# Fritzing sketch pick & place (saved by Fritzing 0.9.9b)

parts:
  Part1 = Arduino Nano (Rev3.0) (ICSP)
  W5500_Module1 = W5500 Ethernet module [package="DIP (Dual Inline) [THT]"]
  Relay = RELAY [package=relay-g5q]
  U2 = Sharp PC817 [package=THT]
  LED1 = LED - 3mm [color="Red (633nm)" current=0.030 package="3 mm [THT]"]
  R4 = Resistor [tolerance=±5% resistance=100 power=0.25 package=THT]
  D1 = Diode [package=diode-1n4001]
  STEP_DOWN_5V = RioRand LM2596
  S1 = SWITCH-MOMENTARY-2 [package=tactile_switch_smd]
  S2 = SWITCH-MOMENTARY-2 [package=tactile_switch_smd]
  JP_VALVE = Header 2 [package=molex-1x2_lock]
  JP_24V_IN = Header 2 [package=molex-1x2_lock]
  R6 = Resistor [tolerance=±5% resistance=10k power=0.25 package=THT]
  JP_SERVO = Header 3 [package=molex-1x3_lock]
  JP_SENSOR = Header 3 [package=molex-1x3_lock]
  LED2 = LED - 3mm [color="Red (633nm)" current=0.030 package="3 mm [THT]"]

nets:
  GND: Part1.GND, W5500_Module1.GND, U2.Pin_2, STEP_DOWN_5V.Pin_4, R6.Pin_1, JP_SERVO.1
  N1: Part1.D3, JP_SERVO.3
  N2: Part1.D4, S1.1
  N3: Part1.D5, S2.1
  N4: Part1.D6, R6.Pin_0, LED2.cathode
  N5: Part1.D7, R4.Pin_0
  N6: Part1.D10, W5500_Module1.SCS
  N7: Part1.D11/MOSI, W5500_Module1.MOSI
  N8: Part1.D12/MISO, W5500_Module1.MISO
  5V: Part1.5V, W5500_Module1.5V, Relay.MAIN, STEP_DOWN_5V.Pin_3, S1.2, S2.2, JP_SERVO.2
  N9: Part1.D13/SCK, W5500_Module1.SCLK
  N10: Relay.COIL2, D1.C, JP_SENSOR.1
  N11: Relay.NO, LED2.anode
  N12: Relay.COIL1, D1.A, STEP_DOWN_5V.Pin_2, JP_VALVE.2, JP_24V_IN.2, JP_SENSOR.2
  N13: U2.Pin_1, LED1.cathode
  N14: U2.Pin_4, STEP_DOWN_5V.Pin_1, JP_24V_IN.1, JP_SENSOR.3
  N15: U2.Pin_3, JP_VALVE.1
  N16: LED1.anode, R4.Pin_1

custom parts:
  W5500 Ethernet module: W5500 based SPI Ethernet module for Arduino, etc.
